// Logisim project counter.circ as structural Verilog: 4 circuits, main circuit RS
module RS (
  input  R,
  input  C,
  input  S,
  output Q,
  output NQ
);

  wire and_1_out, and_2_out, nor_2_out, por_1_out;

  and and_1 (and_1_out, R, C);
  and and_2 (and_2_out, C, S);
  nor nor_1 (Q, and_1_out, NQ);
  nor nor_2 (nor_2_out, Q, and_2_out);
  POR por_1 (.out(por_1_out));
  or or_1 (NQ, nor_2_out, por_1_out);
endmodule

module JK (
  input  K,
  input  C,
  input  J,
  output Q,
  output NQ
);

  wire and_1_out, and_2_out, not_1_out, rs_1_nq, rs_1_q;

  and and_1 (and_1_out, Q, K);
  and and_2 (and_2_out, J, NQ);
  not not_1 (not_1_out, C);
  RS rs_1 (.R(and_1_out), .C(C), .S(and_2_out), .Q(rs_1_q), .NQ(rs_1_nq));
  RS rs_2 (.R(rs_1_nq), .C(not_1_out), .S(rs_1_q), .Q(Q), .NQ(NQ));
endmodule

module SSC (
  input  clock,
  output Q0,
  output Q1,
  output Q2,
  output Q3
);

  wire and_1_out, and_2_out, and_3_out, and_4_out, and_5_out, and_6_out, and_7_out, and_8_out, and_9_out,
       jk_1_nq, jk_1_q, jk_2_nq, jk_2_q, jk_3_nq, jk_3_q, jk_4_nq, not_1_out, not_3_out, not_5_out, or_1_out,
       or_2_out, or_3_out, or_4_out;

  and and_1 (and_1_out, not_1_out, 1'b1);
  not not_1 (not_1_out, and_9_out);
  or or_1 (or_1_out, and_9_out, 1'b1);
  and and_2 (and_2_out, not_1_out, jk_1_q);
  JK jk_1 (.K(or_1_out), .C(clock), .J(and_1_out), .Q(jk_1_q), .NQ(jk_1_nq));
  not not_2 (Q0, jk_1_nq);
  or or_2 (or_2_out, and_9_out, jk_1_q);
  not not_3 (not_3_out, Q0);
  JK jk_2 (.K(or_2_out), .C(clock), .J(and_2_out), .Q(jk_2_q), .NQ(jk_2_nq));
  not not_4 (Q1, jk_2_nq);
  and and_3 (and_3_out, jk_1_q, jk_2_q);
  not not_5 (not_5_out, Q1);
  and and_4 (and_4_out, not_1_out, and_3_out);
  or or_3 (or_3_out, and_9_out, and_3_out);
  and and_5 (and_5_out, not_5_out, not_3_out);
  not not_6 (Q2, jk_3_nq);
  JK jk_3 (.K(or_3_out), .C(clock), .J(and_4_out), .Q(jk_3_q), .NQ(jk_3_nq));
  and and_6 (and_6_out, Q2, and_5_out);
  and and_7 (and_7_out, not_1_out, and_8_out);
  or or_4 (or_4_out, and_9_out, and_8_out);
  and and_8 (and_8_out, and_3_out, jk_3_q);
  not not_7 (Q3, jk_4_nq);
  and and_9 (and_9_out, Q3, and_6_out);
  JK jk_4 (.K(or_4_out), .C(clock), .J(and_7_out), .NQ(jk_4_nq));  // open: Q
endmodule

module main (
  input  in_1,
  output out_2,
  output out_3,
  output out_4,
  output out_5
);

  SSC ssc_1 (.clock(in_1), .Q0(out_2), .Q1(out_3), .Q2(out_4), .Q3(out_5));
endmodule
