// Logisim project lfsg.circ as structural Verilog: 5 circuits, main circuit main
module main (
  input  in_1,
  input  in_2,
  output out_3,
  output out_4,
  output out_5,
  output out_6,
  output out_7,
  output out_8,
  output out_9,
  output out_10,
  output out_11
);

  registr registr_1 (
    .INP(in_1), .clock(in_2), .Q5(out_8), .Q4(out_7), .Q3(out_6), .Q2(out_5), .Q1(out_4), .Q0(out_3),
    .Q8(out_11), .Q7(out_10), .Q6(out_9));
endmodule

module MyTrigger (
  input  D,
  input  C,
  output Q
);

  wire dtrigger_1_q, not_1_out;

  not not_1 (not_1_out, C);
  Dtrigger dtrigger_1 (.D(D), .C(C), .Q(dtrigger_1_q));  // open: NQ
  Dtrigger dtrigger_2 (.D(dtrigger_1_q), .C(not_1_out), .Q(Q));  // open: NQ
endmodule

module RStrigger (
  input  R,
  input  C,
  input  S,
  output Q,
  output NQ
);

  wire and_1_out, and_2_out, nor_2_out, por_1_out;

  and and_1 (and_1_out, R, C);
  and and_2 (and_2_out, C, S);
  POR por_1 (.out(por_1_out));
  nor nor_1 (Q, and_1_out, NQ);
  nor nor_2 (nor_2_out, Q, and_2_out);
  or or_1 (NQ, nor_2_out, por_1_out);
endmodule

module registr (
  input  INP,
  input  clock,
  output Q0,
  output Q1,
  output Q8,
  output Q7,
  output Q6,
  output Q5,
  output Q4,
  output Q3,
  output Q2
);

  wire or_1_out, xor_1_out, xor_2_out, xor_3_out;

  MyTrigger mytrigger_1 (.D(or_1_out), .C(clock), .Q(Q8));
  MyTrigger mytrigger_2 (.D(Q8), .C(clock), .Q(Q7));
  xor xor_1 (xor_1_out, or_1_out, Q7);
  MyTrigger mytrigger_3 (.D(xor_1_out), .C(clock), .Q(Q6));
  xor xor_2 (xor_2_out, or_1_out, Q6);
  MyTrigger mytrigger_4 (.D(xor_2_out), .C(clock), .Q(Q5));
  xor xor_3 (xor_3_out, or_1_out, Q5);
  MyTrigger mytrigger_5 (.D(xor_3_out), .C(clock), .Q(Q4));
  MyTrigger mytrigger_6 (.D(Q4), .C(clock), .Q(Q3));
  MyTrigger mytrigger_7 (.D(Q3), .C(clock), .Q(Q2));
  MyTrigger mytrigger_8 (.D(Q2), .C(clock), .Q(Q1));
  MyTrigger mytrigger_9 (.D(Q1), .C(clock), .Q(Q0));
  or or_1 (or_1_out, INP, Q0);
endmodule

module Dtrigger (
  input  D,
  input  C,
  output Q,
  output NQ
);

  wire not_1_out;

  not not_1 (not_1_out, D);
  RStrigger rstrigger_1 (.R(not_1_out), .C(C), .S(D), .Q(Q), .NQ(NQ));
endmodule
